// Logisim project DataPath.circ as structural Verilog: 2 circuits, main circuit main
module main (
);

  wire and_1_out, and_2_out, clock_1_out, main_1_alusrc, main_1_branch, main_1_branchnot, main_1_jump,
       main_1_memread, main_1_memtoreg, main_1_memwrite, main_1_regdst, main_1_regwrite, main_1_shift,
       mips_alu_1_p4, mips_alu_4_bit_1_p4, or_1_out;
  wire [3:0] main_1_aluop0, multiplexer_1_out, rom_1_data;
  wire [7:0] adder_1_out, adder_2_out, demultiplexer_1_out0, demultiplexer_1_out1, demultiplexer_2_out0,
       demultiplexer_2_out1, mips_alu_1_p5, multiplexer_4_out, multiplexer_5_out, multiplexer_6_out,
       multiplexer_7_out, ram_1_data, ram_2_data, register_1_q, registers_1_read_data1,
       registers_1_read_data2;
  wire [15:0] rom_1_data_2;
  wire [31:0] bit_extender_1_out, bit_extender_2_out, bit_extender_3_out, bit_extender_4_out,
       multiplexer_2_out, multiplexer_3_out;
  wire [31:8] mips_alu_1_p5_2;

  Register register_1 (.D(multiplexer_5_out), .Q(register_1_q), .clk(clock_1_out));  // open: en, clr
  Clock clock_1 (.out(clock_1_out));
  Main main_1 (
    .ABCD(rom_1_data), .RegDst(main_1_regdst), .Branch(main_1_branch), .BranchNot(main_1_branchnot),
    .MemRead(main_1_memread), .MemWrite(main_1_memwrite), .MemtoReg(main_1_memtoreg),
    .ALUOp2(main_1_aluop0[2]), .ALUOp1(main_1_aluop0[1]), .ALUOp0(main_1_aluop0[0]), .ALUSrc(main_1_alusrc),
    .RegWrite(main_1_regwrite), .Shift(main_1_shift), .ALUOp3(main_1_aluop0[3]), .Jump(main_1_jump));
  Adder adder_1 (.a(register_1_q), .b(8'h1), .out(adder_1_out));  // open: cin, cout
  ROM #(.dataWidth(20)) rom_1 (.addr(register_1_q), .data({rom_1_data, rom_1_data_2}));  // open: sel
  Multiplexer #(.width(4), .enable("false")) multiplexer_1 (
    .in0(rom_1_data_2[7:4]), .in1(rom_1_data_2[11:8]), .out(multiplexer_1_out), .sel(main_1_regdst));
  and and_1 (and_1_out, main_1_branchnot, ~mips_alu_1_p4);  // AND_Gate
  and and_2 (and_2_out, main_1_branch, mips_alu_1_p4);
  assign bit_extender_1_out = {{28{1'b0}}, rom_1_data_2[3:0]};  // Bit_Extender bit_extender_1
  assign bit_extender_2_out = {{24{rom_1_data_2[7]}}, rom_1_data_2[7:0]};  // Bit_Extender bit_extender_2
  Registers registers_1 (
    .Read_Register1(rom_1_data_2[15:12]), .Write_Data(multiplexer_7_out), .Write_Register(multiplexer_1_out),
    .Read_Register2(rom_1_data_2[11:8]), .Read_Data1(registers_1_read_data1),
    .Read_Data2(registers_1_read_data2), .RegWrite(main_1_regwrite), .Clock(clock_1_out));
  or or_1 (or_1_out, and_1_out, and_2_out);
  assign bit_extender_3_out = {{24{1'b0}}, registers_1_read_data1};  // Bit_Extender bit_extender_3
  assign bit_extender_4_out = {{24{1'b0}}, registers_1_read_data2};  // Bit_Extender bit_extender_4
  Multiplexer #(.width(32), .enable("false")) multiplexer_2 (
    .in0(bit_extender_4_out), .in1(bit_extender_2_out), .out(multiplexer_2_out), .sel(main_1_alusrc));
  Multiplexer #(.width(32), .enable("false")) multiplexer_3 (
    .in0(bit_extender_3_out), .in1(bit_extender_1_out), .out(multiplexer_3_out), .sel(main_1_shift));
  // MIPS_ALU mips_alu_1: pin names not known; wires that end beside it: multiplexer_3_out, multiplexer_2_out, main_1_aluop0, mips_alu_1_p4, {mips_alu_1_p5_2, mips_alu_1_p5}, {mips_alu_1_p5_2, mips_alu_1_p5}, main_1_memread
  Demultiplexer #(.width(8), .enable("false")) demultiplexer_1 (
    .out0(demultiplexer_1_out0), .out1(demultiplexer_1_out1), .in(mips_alu_1_p5), .sel(mips_alu_4_bit_1_p4));
  Demultiplexer #(.width(8), .enable("false")) demultiplexer_2 (
    .out0(demultiplexer_2_out0), .out1(demultiplexer_2_out1), .in(registers_1_read_data2),
    .sel(mips_alu_4_bit_1_p4));
  Adder adder_2 (.a(adder_1_out), .b(bit_extender_2_out[7:0]), .out(adder_2_out));  // open: cin, cout
  Multiplexer #(.width(8), .enable("false")) multiplexer_4 (
    .in0(adder_1_out), .in1(adder_2_out), .out(multiplexer_4_out), .sel(or_1_out));
  Multiplexer #(.width(8), .enable("false")) multiplexer_5 (
    .in0(multiplexer_4_out), .in1(rom_1_data_2[15:8]), .out(multiplexer_5_out), .sel(main_1_jump));
  RAM #(.bus("separate")) ram_1 (
    .addr(demultiplexer_1_out0), .din(demultiplexer_2_out0), .data(ram_1_data), .str(main_1_memwrite),
    .clk(clock_1_out), .ld(main_1_memread));  // open: sel, clr
  RAM #(.bus("separate")) ram_2 (
    .addr(demultiplexer_1_out1), .din(demultiplexer_2_out1), .data(ram_2_data), .str(main_1_memwrite),
    .clk(clock_1_out), .ld(main_1_memread));  // open: sel, clr
  Multiplexer #(.width(8), .enable("false")) multiplexer_6 (
    .in0(mips_alu_1_p5), .in1(ram_1_data), .out(multiplexer_6_out), .sel(main_1_memtoreg));
  // MIPS_ALU_4_bit mips_alu_4_bit_1: pin names not known; wires that end beside it: rom_1_data_2[15:12], 4'b0110, 4'b0110, mips_alu_4_bit_1_p4
  Multiplexer #(.width(8), .enable("false")) multiplexer_7 (
    .in0(multiplexer_6_out), .in1(ram_2_data), .out(multiplexer_7_out), .sel(mips_alu_4_bit_1_p4));

  // Notes on the sheet:
  //   contents of rom_1 (hex, n*v repeats v):
  //   b1103 c6100 a6200 90112 30112 c0164 a0264 f2201 a0364 f3301 72302 64303 e2304 54320 24508 3220 d3220
  //   13020 40400
endmodule

module Registers (
  input  [3:0] Read_Register1,
  input  [7:0] Write_Data,
  input  RegWrite,
  input  [3:0] Write_Register,
  input  [3:0] Read_Register2,
  input  Clock,
  output [7:0] Read_Data1,
  output [7:0] Read_Data2
);

  wire demultiplexer_2_out0, demultiplexer_2_out1, demultiplexer_2_out2, demultiplexer_2_out3,
       demultiplexer_2_out4, demultiplexer_2_out5, demultiplexer_2_out6, demultiplexer_2_out7;
  wire [7:0] demultiplexer_1_out0, demultiplexer_1_out1, demultiplexer_1_out2, demultiplexer_1_out3,
       demultiplexer_1_out4, demultiplexer_1_out5, demultiplexer_1_out6, demultiplexer_1_out7, register_1_q,
       register_2_q, register_3_q, register_4_q, register_5_q, register_6_q, register_7_q, register_8_q;

  Demultiplexer #(.select(4), .width(8), .enable("false")) demultiplexer_1 (
    .out0(demultiplexer_1_out0), .out1(demultiplexer_1_out1), .out2(demultiplexer_1_out2),
    .out3(demultiplexer_1_out3), .out4(demultiplexer_1_out4), .out5(demultiplexer_1_out5),
    .out6(demultiplexer_1_out6), .out7(demultiplexer_1_out7), .in(Write_Data), .sel(Write_Register));  // open: out8, out9, out10, out11, out12, out13, out14, out15
  Demultiplexer #(.select(4), .enable("false")) demultiplexer_2 (
    .out0(demultiplexer_2_out0), .out1(demultiplexer_2_out1), .out2(demultiplexer_2_out2),
    .out3(demultiplexer_2_out3), .out4(demultiplexer_2_out4), .out5(demultiplexer_2_out5),
    .out6(demultiplexer_2_out6), .out7(demultiplexer_2_out7), .in(RegWrite), .sel(Write_Register));  // open: out8, out9, out10, out11, out12, out13, out14, out15
  Register register_1 (.D(demultiplexer_1_out0), .en(demultiplexer_2_out0), .Q(register_1_q), .clk(Clock), .clr(1'b0));
  Register register_2 (.D(demultiplexer_1_out1), .en(demultiplexer_2_out1), .Q(register_2_q), .clk(Clock), .clr(1'b0));
  Register register_3 (.D(demultiplexer_1_out2), .en(demultiplexer_2_out2), .Q(register_3_q), .clk(Clock), .clr(1'b0));
  Register register_4 (.D(demultiplexer_1_out3), .en(demultiplexer_2_out3), .Q(register_4_q), .clk(Clock), .clr(1'b0));
  Register register_5 (.D(demultiplexer_1_out4), .en(demultiplexer_2_out4), .Q(register_5_q), .clk(Clock), .clr(1'b0));
  Register register_6 (.D(demultiplexer_1_out5), .en(demultiplexer_2_out5), .Q(register_6_q), .clk(Clock), .clr(1'b0));
  Register register_7 (.D(demultiplexer_1_out6), .en(demultiplexer_2_out6), .Q(register_7_q), .clk(Clock), .clr(1'b0));
  Register register_8 (.D(demultiplexer_1_out7), .en(demultiplexer_2_out7), .Q(register_8_q), .clk(Clock), .clr(1'b0));
  Multiplexer #(.select(4), .width(8), .enable("false")) multiplexer_1 (
    .in0(register_1_q), .in1(register_2_q), .in2(register_3_q), .in3(register_4_q), .in4(register_5_q),
    .in5(register_6_q), .in6(register_7_q), .in7(register_8_q), .out(Read_Data1), .sel(Read_Register1));  // open: in8, in9, in10, in11, in12, in13, in14, in15
  Multiplexer #(.select(4), .width(8), .enable("false")) multiplexer_2 (
    .in0(register_1_q), .in1(register_2_q), .in2(register_3_q), .in3(register_4_q), .in4(register_5_q),
    .in5(register_6_q), .in6(register_7_q), .in7(register_8_q), .out(Read_Data2), .sel(Read_Register2));  // open: in8, in9, in10, in11, in12, in13, in14, in15
endmodule
