// Logisim project diku.circ as structural Verilog: 15 circuits, main circuit Main
module RegDst (
  input  [3:0] ABCD,
  output RegDst
);

  wire and_1_out, and_2_out;

  and and_1 (and_1_out, ~ABCD[0], ABCD[1]);  // AND_Gate
  and and_2 (and_2_out, ABCD[1], ABCD[3]);
  or or_1 (RegDst, and_1_out, and_2_out);
endmodule

module Branch (
  input  [3:0] ABCD,
  output Branch
);

  and and_1 (Branch, ~ABCD[3], ABCD[2], ABCD[1], ABCD[0]);  // AND_Gate
endmodule

module BranchNot (
  input  [3:0] ABCD,
  output BranchNot
);

  and and_1 (BranchNot, ~ABCD[0], ABCD[1], ~ABCD[2], ~ABCD[3]);  // AND_Gate
endmodule

module MemRead (
  input  [3:0] ABCD,
  output MemRead
);

  and and_1 (MemRead, ~ABCD[0], ABCD[1], ~ABCD[2], ABCD[3]);  // AND_Gate
endmodule

module MemWrite (
  input  [3:0] ABCD,
  output MemWrite
);

  and and_1 (MemWrite, ~ABCD[0], ~ABCD[1], ABCD[2], ABCD[3]);  // AND_Gate
endmodule

module MemtoReg (
  input  [3:0] ABCD,
  output MemtoReg
);

  and and_1 (MemtoReg, ~ABCD[0], ABCD[1], ~ABCD[2]);  // AND_Gate
endmodule

module ALUOp3 (
  input  [3:0] ABCD,
  output ALUOp3
);

  wire and_1_out, and_2_out, and_3_out;

  and and_1 (and_1_out, ~ABCD[1], ABCD[2], ~ABCD[3]);  // AND_Gate
  and and_2 (and_2_out, ABCD[0], ABCD[1], ~ABCD[2], ~ABCD[3]);  // AND_Gate
  and and_3 (and_3_out, ABCD[0], ~ABCD[1], ~ABCD[2], ABCD[3]);  // AND_Gate
  or or_1 (ALUOp3, and_1_out, and_2_out, and_3_out);
endmodule

module ALUOp2 (
  input  [3:0] ABCD,
  output ALUOp2
);

  wire and_1_out, and_2_out, and_3_out, and_4_out;

  and and_1 (and_1_out, ABCD[0], ABCD[2], ~ABCD[3]);  // AND_Gate
  and and_2 (and_2_out, ABCD[0], ABCD[1], ABCD[2]);
  and and_3 (and_3_out, ~ABCD[0], ABCD[1], ~ABCD[2], ~ABCD[3]);  // AND_Gate
  and and_4 (and_4_out, ~ABCD[0], ~ABCD[1], ~ABCD[2], ABCD[3]);  // AND_Gate
  or or_1 (ALUOp2, and_1_out, and_2_out, and_3_out, and_4_out);
endmodule

module ALUOp1 (
  input  [3:0] ABCD,
  output ALUOp1
);

  wire and_1_out, and_2_out, and_3_out, and_4_out;

  and and_1 (and_1_out, ~ABCD[0], ~ABCD[2]);  // AND_Gate
  and and_2 (and_2_out, ~ABCD[0], ~ABCD[1]);  // AND_Gate
  and and_3 (and_3_out, ABCD[0], ABCD[1], ABCD[2]);
  and and_4 (and_4_out, ABCD[1], ~ABCD[2], ABCD[3]);  // AND_Gate
  or or_1 (ALUOp1, and_1_out, and_2_out, and_3_out, and_4_out);
endmodule

module ALUOp0 (
  input  [3:0] ABCD,
  output ALUOp0
);

  wire and_1_out, and_2_out;

  and and_1 (and_1_out, ABCD[0], ~ABCD[2], ~ABCD[3]);  // AND_Gate
  and and_2 (and_2_out, ABCD[3], ABCD[2], ABCD[1], ~ABCD[0]);  // AND_Gate
  or or_1 (ALUOp0, and_1_out, and_2_out);
endmodule

module ALUSrc (
  input  [3:0] ABCD,
  output ALUSrc
);

  wire and_1_out, and_2_out;

  and and_1 (and_1_out, ~ABCD[0], ABCD[2]);  // AND_Gate
  and and_2 (and_2_out, ABCD[1], ABCD[3]);
  or or_1 (ALUSrc, and_1_out, and_2_out);
endmodule

module RegWrite (
  input  [3:0] ABCD,
  output RegWrite
);

  wire and_1_out, and_2_out, and_3_out, and_4_out, and_5_out;

  and and_1 (and_1_out, ~ABCD[1], ~ABCD[2]);  // AND_Gate
  and and_2 (and_2_out, ABCD[0], ~ABCD[2]);  // AND_Gate
  and and_3 (and_3_out, ABCD[0], ~ABCD[1]);  // AND_Gate
  and and_4 (and_4_out, ABCD[1], ABCD[3]);
  and and_5 (and_5_out, ~ABCD[0], ABCD[1], ABCD[2]);  // AND_Gate
  or or_1 (RegWrite, and_1_out, and_2_out, and_3_out, and_4_out, and_5_out);
endmodule

module Shift (
  input  [3:0] ABCD,
  output Shift
);

  wire and_1_out, and_2_out;

  and and_1 (and_1_out, ABCD[0], ABCD[1], ~ABCD[2], ~ABCD[3]);  // AND_Gate
  and and_2 (and_2_out, ABCD[3], ~ABCD[2], ~ABCD[1], ABCD[0]);  // AND_Gate
  or or_1 (Shift, and_1_out, and_2_out);
endmodule

module Main (
  input  [3:0] ABCD,
  output RegDst,
  output Branch,
  output BranchNot,
  output MemRead,
  output MemWrite,
  output MemtoReg,
  output ALUOp3,
  output ALUOp2,
  output ALUOp1,
  output ALUOp0,
  output ALUSrc,
  output RegWrite,
  output Shift,
  output Jump
);

  RegDst u_RegDst (.ABCD(ABCD), .RegDst(RegDst));
  Branch u_Branch (.ABCD(ABCD), .Branch(Branch));
  BranchNot u_BranchNot (.ABCD(ABCD), .BranchNot(BranchNot));
  MemRead u_MemRead (.ABCD(ABCD), .MemRead(MemRead));
  MemWrite u_MemWrite (.ABCD(ABCD), .MemWrite(MemWrite));
  MemtoReg u_MemtoReg (.ABCD(ABCD), .MemtoReg(MemtoReg));
  ALUOp3 u_ALUOp3 (.ABCD(ABCD), .ALUOp3(ALUOp3));
  ALUOp2 u_ALUOp2 (.ABCD(ABCD), .ALUOp2(ALUOp2));
  ALUOp1 u_ALUOp1 (.ABCD(ABCD), .ALUOp1(ALUOp1));
  ALUOp0 u_ALUOp0 (.ABCD(ABCD), .ALUOp0(ALUOp0));
  ALUSrc u_ALUSrc (.ABCD(ABCD), .ALUSrc(ALUSrc));
  RegWrite u_RegWrite (.ABCD(ABCD), .RegWrite(RegWrite));
  Shift u_Shift (.ABCD(ABCD), .Shift(Shift));
  Jump u_Jump (.in_1(ABCD), .out_2(Jump));
endmodule

module Jump (
  input  [3:0] in_1,
  output out_2
);

  and and_1 (out_2, ~in_1[0], ~in_1[1], in_1[2], ~in_1[3]);  // AND_Gate
endmodule
