// Logisim project Final-Circuit.circ as structural Verilog: 1 circuit, main circuit main
module main (
  input  [3:0] A,
  input  [3:0] B,
  input  [2:0] S,
  output [3:0] OUTPUT,
  output ZF,
  output SF,
  output VF,
  output CF
);

  wire and_1_out, and_2_out, and_3_out, and_4_out, and_5_out, and_6_out, and_7_out, and_8_out, and_9_out,
       and_10_out, and_11_out, and_12_out, and_13_out, CIN_out, not_1_out, not_2_out, not_3_out, not_4_out,
       not_5_out, not_6_out, not_7_out, not_8_out, not_9_out, not_10_out, not_11_out, or_1_out, or_2_out,
       or_3_out, or_4_out, or_5_out, or_6_out, or_7_out, or_8_out, or_9_out, or_10_out, or_11_out, or_12_out,
       X3_out, Y3_out;
  wire [2:0] X0_out, Y0_out;
  wire [3:3] adder_1_out;

  not not_1 (not_1_out, B[0]);
  not not_2 (not_2_out, B[1]);
  not not_3 (not_3_out, B[2]);
  not not_4 (not_4_out, B[3]);
  not not_5 (not_5_out, S[1]);
  not not_6 (not_6_out, S[0]);
  not not_7 (not_7_out, A[0]);
  not not_8 (not_8_out, A[1]);
  not not_9 (not_9_out, A[2]);
  not not_10 (not_10_out, A[3]);
  or or_1 (or_1_out, not_5_out, not_6_out);
  and and_1 (and_1_out, not_5_out, S[0]);
  or or_2 (or_2_out, or_1_out, not_1_out);
  or or_3 (or_3_out, not_6_out, not_7_out);
  or or_4 (or_4_out, or_1_out, not_2_out);
  or or_5 (or_5_out, or_1_out, not_8_out);
  or or_6 (or_6_out, or_1_out, not_3_out);
  or or_7 (or_7_out, not_6_out, not_9_out);
  or or_8 (or_8_out, or_1_out, not_4_out);
  or or_9 (or_9_out, not_6_out, not_10_out);
  and and_2 (and_2_out, A[0], or_2_out);
  and and_3 (and_3_out, B[0], S[1]);
  and and_4 (and_4_out, and_3_out, or_3_out);
  and and_5 (and_5_out, A[1], or_4_out);
  and and_6 (and_6_out, B[1], S[1]);
  and and_7 (and_7_out, and_6_out, or_5_out);
  and and_8 (and_8_out, A[2], or_6_out);
  and and_9 (and_9_out, B[2], S[1]);
  and and_10 (and_10_out, and_9_out, or_7_out);
  and and_11 (and_11_out, A[3], or_8_out);
  and and_12 (and_12_out, B[3], S[1]);
  and and_13 (and_13_out, and_12_out, or_9_out);
  not not_11 (not_11_out, S[1]);
  and Y0 (Y0_out[0], and_1_out, B[0]);
  or X0 (X0_out[0], and_2_out, and_4_out);
  and Y1 (Y0_out[1], and_1_out, B[1]);
  or X1 (X0_out[1], and_5_out, and_7_out);
  and Y2 (Y0_out[2], and_1_out, B[2]);
  or X2 (X0_out[2], and_8_out, and_10_out);
  and Y3 (Y3_out, and_1_out, B[3]);
  or X3 (X3_out, and_11_out, and_13_out);
  and CIN (CIN_out, not_11_out, S[2]);
  Adder #(.width(4)) adder_1 (
    .a({1'b0, Y0_out}), .b({1'b0, X0_out}), .out({adder_1_out[3], OUTPUT[2:0]}), .cin(CIN_out));  // open: cout
  Adder #(.width(1)) adder_2 (.a(Y3_out), .b(X3_out), .out(OUTPUT[3]), .cin(adder_1_out[3]), .cout(CF));
  or or_10 (or_10_out, OUTPUT[0], OUTPUT[1]);
  or or_11 (or_11_out, OUTPUT[2], OUTPUT[3]);
  xor xor_1 (VF, adder_1_out[3], CF);
  or or_12 (or_12_out, or_10_out, or_11_out);
  not not_12 (ZF, or_12_out);

  assign SF = OUTPUT[3];
endmodule
