// Logisim project Final-Circuit.circ as structural Verilog: 5 circuits, main circuit float_adder
// 4 bit ALU
module main (
  input  [3:0] A,
  input  [3:0] B,
  input  [2:0] S,
  input  in_4,
  output [3:0] Output,
  output COUT
);

  wire and_1_out, and_2_out, and_3_out, and_4_out, and_5_out, and_6_out, and_7_out, and_8_out, and_9_out,
       and_10_out, and_11_out, and_12_out, and_13_out, CIN_out, not_1_out, not_2_out, not_3_out, not_4_out,
       not_5_out, not_6_out, not_7_out, not_8_out, not_9_out, not_10_out, not_11_out, or_1_out, or_2_out,
       or_3_out, or_4_out, or_5_out, or_6_out, or_7_out, or_8_out, or_9_out, or_10_out;
  wire [3:0] X0_out, Y0_out;

  not not_1 (not_1_out, B[0]);
  not not_2 (not_2_out, B[1]);
  not not_3 (not_3_out, B[2]);
  not not_4 (not_4_out, B[3]);
  not not_5 (not_5_out, S[1]);
  not not_6 (not_6_out, S[0]);
  not not_7 (not_7_out, A[0]);
  not not_8 (not_8_out, A[1]);
  not not_9 (not_9_out, A[2]);
  not not_10 (not_10_out, A[3]);
  or or_1 (or_1_out, not_5_out, not_6_out);
  and and_1 (and_1_out, not_5_out, S[0]);
  or or_2 (or_2_out, or_1_out, not_1_out);
  or or_3 (or_3_out, not_6_out, not_7_out);
  or or_4 (or_4_out, or_1_out, not_2_out);
  or or_5 (or_5_out, or_1_out, not_8_out);
  or or_6 (or_6_out, or_1_out, not_3_out);
  or or_7 (or_7_out, not_6_out, not_9_out);
  or or_8 (or_8_out, or_1_out, not_4_out);
  or or_9 (or_9_out, not_6_out, not_10_out);
  and and_2 (and_2_out, A[0], or_2_out);
  and and_3 (and_3_out, B[0], S[1]);
  and and_4 (and_4_out, and_3_out, or_3_out);
  and and_5 (and_5_out, A[1], or_4_out);
  and and_6 (and_6_out, B[1], S[1]);
  and and_7 (and_7_out, and_6_out, or_5_out);
  and and_8 (and_8_out, A[2], or_6_out);
  and and_9 (and_9_out, B[2], S[1]);
  and and_10 (and_10_out, and_9_out, or_7_out);
  and and_11 (and_11_out, A[3], or_8_out);
  and and_12 (and_12_out, B[3], S[1]);
  and and_13 (and_13_out, and_12_out, or_9_out);
  not not_11 (not_11_out, S[1]);
  and Y0 (Y0_out[0], and_1_out, B[0]);
  or X0 (X0_out[0], and_2_out, and_4_out);
  and Y1 (Y0_out[1], and_1_out, B[1]);
  or X1 (X0_out[1], and_5_out, and_7_out);
  and Y2 (Y0_out[2], and_1_out, B[2]);
  or X2 (X0_out[2], and_8_out, and_10_out);
  and Y3 (Y0_out[3], and_1_out, B[3]);
  or X3 (X0_out[3], and_11_out, and_13_out);
  and CIN (CIN_out, not_11_out, S[2]);
  or or_10 (or_10_out, CIN_out, in_4);
  Adder #(.width(4)) adder_1 (.a(Y0_out), .b(X0_out), .out(Output), .cin(or_10_out), .cout(COUT));
endmodule

module _16_bit_ALU (
  input  cin,
  input  [15:0] A,
  input  [15:0] B,
  output [15:0] \output ,
  output cout
);

  wire main_1_cout, main_2_cout, main_3_cout;

  main main_1 (.A(A[3:0]), .B(B[3:0]), .S(3'b001), .COUT(main_1_cout), .Output(\output [3:0]), .in_4(cin));
  main main_2 (.A(A[7:4]), .B(B[7:4]), .S(3'b001), .COUT(main_2_cout), .Output(\output [7:4]), .in_4(main_1_cout));
  main main_3 (.A(A[11:8]), .B(B[11:8]), .S(3'b001), .COUT(main_3_cout), .Output(\output [11:8]), .in_4(main_2_cout));
  main main_4 (.A(A[15:12]), .B(B[15:12]), .S(3'b001), .COUT(cout), .Output(\output [15:12]), .in_4(main_3_cout));
endmodule

module float_adder (
  input  [15:0] B,
  input  [15:0] A,
  output [3:0] Exponent,
  output [10:0] Fraction,
  output Overflow
);

  wire and_1_out, and_2_out, n4_bit_s_g_1_o_2, n4_bit_s_s_1_o_2, not_1_out, or_1_out, or_2_out;
  wire [3:0] main_1_output, n4_bit_s_g_1_o, n4_bit_s_s_1_o, negator_1_out;
  wire [10:0] separate_greater_1_out_3, separate_smaller_1_out_3, shifter_2_out;
  wire [11:11] and_3_out;
  wire [12:0] n16_bit_alu_1_output;
  wire [12:11] shifter_2_out_2;
  wire [15:0] shifter_1_out;
  wire [15:11] n16_bit_alu_1_output_2;

  Negator #(.width(4)) negator_1 (.in(n4_bit_s_s_1_o), .out(negator_1_out));
  main main_1 (.A(n4_bit_s_g_1_o), .B(negator_1_out), .S(3'b001), .Output(main_1_output), .in_4(1'b0));  // open: COUT
  Adder #(.width(4)) adder_1 (.a(n4_bit_s_g_1_o), .b(4'b0000), .out(Exponent), .cin(and_1_out), .cout(Overflow));
  _4_bit_s_s u_4_bit_s_s_1 (.in_1(A[14:11]), .in_2(B[14:11]), .O(n4_bit_s_s_1_o), .O_2(n4_bit_s_s_1_o_2));
  _4_bit_s_g u_4_bit_s_g_1 (.in_1(A[14:11]), .in_2(B[14:11]), .O(n4_bit_s_g_1_o), .O_2(n4_bit_s_g_1_o_2));
  or or_1 (or_1_out, n4_bit_s_g_1_o[3], n4_bit_s_g_1_o[2], n4_bit_s_g_1_o[1], n4_bit_s_g_1_o[0]);
  not not_1 (not_1_out, n4_bit_s_s_1_o_2);
  and and_1 (and_1_out, or_1_out, n16_bit_alu_1_output[12]);
  Adder #(.width(11)) adder_2 (.a(shifter_2_out), .b({11{1'b0}}), .out(Fraction), .cin(and_2_out));  // open: cout
  separate_smaller separate_smaller_1 (.X(A), .Y(B), .out_3(separate_smaller_1_out_3));
  Shifter #(.width(16), .shift("lr")) shifter_1 (
    .in({4'b0000, and_3_out[11], separate_smaller_1_out_3}), .\dist (main_1_output), .out(shifter_1_out));
  and and_2 (and_2_out, n16_bit_alu_1_output[12], n16_bit_alu_1_output[0]);
  or or_2 (or_2_out, B[0], B[1], B[2], B[3], B[4], B[5], B[6], B[7], B[8], B[9], B[10], B[11], B[12], B[13], B[14]);
  and and_3 (and_3_out[11], or_2_out, not_1_out);
  _16_bit_ALU u_16_bit_alu_1 (
    .B(shifter_1_out), .A({{5{1'b0}}, separate_greater_1_out_3}), .cin(1'b0),
    .\output ({n16_bit_alu_1_output_2, n16_bit_alu_1_output[10:0]}));  // open: cout
  Adder #(.width(2)) adder_3 (
    .a({1'b0, n16_bit_alu_1_output_2[11]}), .b(2'b01), .out(n16_bit_alu_1_output[12:11]),
    .cin(n4_bit_s_g_1_o_2));  // open: cout
  separate_greater separate_greater_1 (.X(A), .out_3(separate_greater_1_out_3), .Y(B));
  Shifter #(.width(13), .shift("lr")) shifter_2 (
    .in(n16_bit_alu_1_output), .\dist ({3'b000, n16_bit_alu_1_output[12]}),
    .out({shifter_2_out_2, shifter_2_out}));
endmodule

module _4_bit_s_s (
  input  [3:0] in_1,
  input  [3:0] in_2,
  output [3:0] O,
  output O_2
);

  wire comparator_1_a_b;
  wire [3:0] and_1_out, and_2_out;
  wire [3:3] comparator_1_a_b_2, or_1_out;

  comparator comparator_1 (
    .X3(in_1[3]), .Y3(in_2[3]), .X2(in_1[2]), .Y2(in_2[2]), .X1(in_1[1]), .Y1(in_2[1]), .X0(in_1[0]),
    .Y0(in_2[0]), .A_B(comparator_1_a_b), .A_B_2(comparator_1_a_b_2[3]), .A_B_3(O_2));
  or or_1 (or_1_out[3], comparator_1_a_b, O_2);
  assign and_1_out = in_1 & {4{or_1_out[3]}};  // AND_Gate and_1, 4 bits wide
  assign and_2_out = {4{comparator_1_a_b_2[3]}} & in_2;  // AND_Gate and_2, 4 bits wide
  assign O = and_1_out | and_2_out;  // OR_Gate or_2, 4 bits wide
endmodule

module _4_bit_s_g (
  input  [3:0] in_1,
  input  [3:0] in_2,
  output [3:0] O,
  output O_2
);

  wire comparator_1_a_b_2;
  wire [3:0] and_1_out, and_2_out;
  wire [3:3] comparator_1_a_b, or_1_out;

  comparator comparator_1 (
    .X3(in_1[3]), .Y3(in_2[3]), .X2(in_1[2]), .Y2(in_2[2]), .X1(in_1[1]), .Y1(in_2[1]), .X0(in_1[0]),
    .Y0(in_2[0]), .A_B(comparator_1_a_b[3]), .A_B_2(comparator_1_a_b_2), .A_B_3(O_2));
  or or_1 (or_1_out[3], O_2, comparator_1_a_b_2);
  assign and_1_out = in_1 & {4{or_1_out[3]}};  // AND_Gate and_1, 4 bits wide
  assign and_2_out = {4{comparator_1_a_b[3]}} & in_2;  // AND_Gate and_2, 4 bits wide
  assign O = and_1_out | and_2_out;  // OR_Gate or_2, 4 bits wide
endmodule
