// Logisim project comparator.circ as structural Verilog: 4 circuits, main circuit separate smaller
module comparator (
  input  X3,
  input  Y3,
  input  X2,
  input  Y2,
  input  X1,
  input  Y1,
  input  X0,
  input  Y0,
  output A_B,
  output A_B_2,
  output A_B_3
);

  wire and_1_out, and_2_out, and_3_out, and_4_out, and_5_out, and_6_out, nand_seg_1_a_prime_b,
       nand_seg_1_ab_prime, nand_seg_1_y, nand_seg_2_a_prime_b, nand_seg_2_ab_prime, nand_seg_2_y,
       nand_seg_3_a_prime_b, nand_seg_3_ab_prime, nand_seg_3_y, nand_seg_4_a_prime_b, nand_seg_4_ab_prime,
       nand_seg_4_y;

  nand_seg nand_seg_1 (
    .A(X3), .B(Y3), .A_prime_B(nand_seg_1_a_prime_b), .Y(nand_seg_1_y), .AB_prime(nand_seg_1_ab_prime));
  nand_seg nand_seg_2 (
    .A(X2), .B(Y2), .A_prime_B(nand_seg_2_a_prime_b), .Y(nand_seg_2_y), .AB_prime(nand_seg_2_ab_prime));
  nand_seg nand_seg_3 (
    .A(X1), .B(Y1), .A_prime_B(nand_seg_3_a_prime_b), .Y(nand_seg_3_y), .AB_prime(nand_seg_3_ab_prime));
  nand_seg nand_seg_4 (
    .A(X0), .B(Y0), .A_prime_B(nand_seg_4_a_prime_b), .Y(nand_seg_4_y), .AB_prime(nand_seg_4_ab_prime));
  and and_1 (and_1_out, nand_seg_1_y, nand_seg_2_a_prime_b);
  and and_2 (and_2_out, nand_seg_1_y, nand_seg_2_ab_prime);
  and and_3 (and_3_out, nand_seg_1_y, nand_seg_2_y, nand_seg_3_a_prime_b);
  and and_4 (and_4_out, nand_seg_1_y, nand_seg_2_y, nand_seg_3_ab_prime);
  and and_5 (and_5_out, nand_seg_1_y, nand_seg_2_y, nand_seg_3_y, nand_seg_4_a_prime_b);
  and and_6 (and_6_out, nand_seg_1_y, nand_seg_2_y, nand_seg_3_y, nand_seg_4_ab_prime);
  or or_1 (A_B, nand_seg_1_a_prime_b, and_1_out, and_3_out, and_5_out);
  or or_2 (A_B_2, nand_seg_1_ab_prime, and_2_out, and_4_out, and_6_out);
  and and_7 (A_B_3, nand_seg_1_y, nand_seg_2_y, nand_seg_3_y, nand_seg_4_y);
endmodule

module nand_seg (
  input  A,
  input  B,
  output A_prime_B,
  output Y,
  output AB_prime
);

  wire not_1_out, not_2_out;

  not not_1 (not_1_out, A);
  not not_2 (not_2_out, B);
  and and_1 (A_prime_B, not_1_out, B);
  and and_2 (AB_prime, A, not_2_out);
  nor nor_1 (Y, A_prime_B, AB_prime);
endmodule

module separate_smaller (
  input  [15:0] X,
  input  [15:0] Y,
  output [10:0] out_3
);

  wire comparator_1_a_b_2, comparator_1_a_b_3;
  wire [10:0] and_1_out, and_2_out;
  wire [10:10] comparator_1_a_b, or_1_out;

  comparator comparator_1 (
    .X3(X[14]), .Y3(Y[14]), .X2(X[13]), .Y2(Y[13]), .X1(X[12]), .Y1(Y[12]), .X0(X[11]), .Y0(Y[11]),
    .A_B(comparator_1_a_b[10]), .A_B_2(comparator_1_a_b_2), .A_B_3(comparator_1_a_b_3));
  or or_1 (or_1_out[10], comparator_1_a_b_3, comparator_1_a_b_2);
  assign and_1_out = X[10:0] & {11{comparator_1_a_b[10]}};  // AND_Gate and_1, 11 bits wide
  assign and_2_out = {11{or_1_out[10]}} & Y[10:0];  // AND_Gate and_2, 11 bits wide
  assign out_3 = and_1_out | and_2_out;  // OR_Gate or_2, 11 bits wide
endmodule

module separate_greater (
  input  [15:0] X,
  input  [15:0] Y,
  output [10:0] out_3
);

  wire comparator_1_a_b_2, comparator_1_a_b_3;
  wire [10:0] and_1_out, and_2_out;
  wire [10:10] comparator_1_a_b, or_1_out;

  comparator comparator_1 (
    .X3(X[14]), .Y3(Y[14]), .X2(X[13]), .Y2(Y[13]), .X1(X[12]), .Y1(Y[12]), .X0(X[11]), .Y0(Y[11]),
    .A_B(comparator_1_a_b[10]), .A_B_2(comparator_1_a_b_2), .A_B_3(comparator_1_a_b_3));
  or or_1 (or_1_out[10], comparator_1_a_b_3, comparator_1_a_b_2);
  assign and_1_out = X[10:0] & {11{or_1_out[10]}};  // AND_Gate and_1, 11 bits wide
  assign and_2_out = {11{comparator_1_a_b[10]}} & Y[10:0];  // AND_Gate and_2, 11 bits wide
  assign out_3 = and_1_out | and_2_out;  // OR_Gate or_2, 11 bits wide
endmodule
